# Fritzing sketch PerfBoard (saved by Fritzing 0.8.7b)
perfboards: 1

parts:
  Composant1 = Arduino Pro Mini v13
  Composant2 = SRF05 Ultrasonic Rangefinder
  J1 = Piezo Speaker
  U1 = SWITCH_SPDT [package=kps-1290]
  BAT1 = BC9VPC [package=bc9vpc]
  LED1 = LED - 5mm [color="Red (633nm)" package="5 mm [THT]"]
  R1 = Resistor [tolerance=±5% resistance=150 package=THT]
  R2 = Resistor [tolerance=±5% resistance=220 package=THT]
  LED2 = LED - 5mm [color="Red (633nm)" package="5 mm [THT]"]  # not connected

nets:
  N1: Composant1.RAW, BAT1.V-
  GND: Composant1.GND, Composant2.GND, J1.pin1
  N2: Composant1.A3, J1.pin2
  N3: Composant1.D11_PWM/MOSI, R2.Pin_0
  N4: Composant1.D10_PWM/SS, LED1.anode
  N5: U1.P, BAT1.V+
  N6: LED1.cathode, R1.Pin_0
