# Fritzing sketch SquatCheck (saved by Fritzing 0.8.7b)
breadboards: 1

parts:
  S1 = Square Pushbutton
  LED1 = LED - 5mm [color="Red (633nm)" part_number="Status (Laser)" package="5 mm [THT]"]
  R1 = Resistor [tolerance=±5% resistance=220 package=THT]
  Ping_Ultrasound_sensor = SRF05 Ultrasonic Rangefinder
  R2 = Resistor [tolerance=±5% resistance=220 package=THT]
  LED2 = LED - 3mm [color="Red (633nm)" part_number=POWER package="3 mm [THT]"]
  Arduino_Pro_Mini = Arduino Pro Mini v13
  VCC1 = Battery block 9V
  J1 = Piezo Speaker

nets:
  N1: S1.leg0, VCC1.-
  GND: S1.leg1, LED1.cathode, Ping_Ultrasound_sensor.GND, LED2.cathode, Arduino_Pro_Mini.GND, J1.pin1
  N2: LED1.anode, R1.Pin_1
  N3: R1.Pin_0, Arduino_Pro_Mini.D2
  N4: Ping_Ultrasound_sensor.VCC, Arduino_Pro_Mini.D9_PWM
  N5: Ping_Ultrasound_sensor.Trig, Arduino_Pro_Mini.D5_PWM
  N6: Ping_Ultrasound_sensor.Echo, Arduino_Pro_Mini.D4
  N7: R2.Pin_0, Arduino_Pro_Mini.D11_PWM/MOSI
  N8: R2.Pin_1, LED2.anode
  N9: Arduino_Pro_Mini.RAW, VCC1.+
  N10: Arduino_Pro_Mini.D8, J1.pin2
